// Logisim project CS1503_U201514559_周铭昊_CPU.circ as structural Verilog: 2 circuits, main circuit cpu
module cpu (
);

  wire alu_1_p4, ALUsrc, and_1_out, and_2_out, and_3_out, beq, blez, bne, CLK, comparator_1_gt, EXTOP, j,
       jal, jr, MemToReg, Memwrite, not_1_out, not_2_out, or_1_out, or_2_out, RegDst, RegWrite, RST;
  wire [3:0] ALUOP;
  wire [4:0] multiplexer_1_out, multiplexer_3_out;
  wire [15:0] PC_q, \总周期数 , \无条件分支指令数 , \有条件分支成功跳转 , \有条件分支指令数 ;
  wire [31:0] adder_1_out, adder_2_out, alu_1_p5, bit_extender_1_out, bit_extender_2_out, multiplexer_2_out,
       multiplexer_4_out, multiplexer_5_out, multiplexer_6_out, multiplexer_7_out, multiplexer_8_out,
       multiplexer_9_out, PC31__28__instr_index__02, ram_1_data, registerfile_1_p7, RF_A, rom_1_data,
       shifter_1_out, SyscallOut;
  wire [31:16] PC_q_2;

  Button \u_总复位  (.out(RST));
  Clock clock_1 (.out(CLK));
  Register #(.width(32)) PC (.D(multiplexer_5_out), .Q({PC_q_2, PC_q}));  // open: en, clk, clr
  Hex_Digit_Display hex_digit_display_1 (.value(SyscallOut[31:28]));  // open: dp
  Hex_Digit_Display hex_digit_display_2 (.value(SyscallOut[27:24]));  // open: dp
  Adder #(.width(32)) adder_1 (.a(32'h4), .b({PC_q_2, PC_q}), .out(adder_1_out));  // open: cin, cout
  Hex_Digit_Display hex_digit_display_3 (.value(SyscallOut[19:16]));  // open: dp
  Hex_Digit_Display hex_digit_display_4 (.value(SyscallOut[23:20]));  // open: dp
  ROM #(.addrWidth(16), .dataWidth(32)) rom_1 (.addr(PC_q), .data(rom_1_data));  // open: sel
  Hex_Digit_Display hex_digit_display_5 (.value(SyscallOut[15:12]));  // open: dp
  Hex_Digit_Display hex_digit_display_6 (.value(SyscallOut[11:8]));  // open: dp
  // Probe on rom_1_data[31:26]
  // Probe on rom_1_data[5:0]
  Hex_Digit_Display hex_digit_display_7 (.value(SyscallOut[3:0]));  // open: dp
  Hex_Digit_Display hex_digit_display_8 (.value(SyscallOut[7:4]));  // open: dp
  // Probe on \总周期数 
  // Probe on \无条件分支指令数 
  // Probe on \有条件分支指令数 
  // Probe on \有条件分支成功跳转 
  Multiplexer #(.width(5), .enable("false")) multiplexer_1 (
    .in0(rom_1_data[20:16]), .in1(rom_1_data[15:11]), .out(multiplexer_1_out), .sel(RegDst));
  assign bit_extender_1_out = {{16{rom_1_data[15]}}, rom_1_data[15:0]};  // Bit_Extender bit_extender_1
  assign bit_extender_2_out = {{16{1'b0}}, rom_1_data[15:0]};  // Bit_Extender bit_extender_2
  Multiplexer #(.width(32), .enable("false")) multiplexer_2 (
    .in0(multiplexer_8_out), .in1(adder_1_out), .out(multiplexer_2_out), .sel(jal));
  Multiplexer #(.width(5), .enable("false")) multiplexer_3 (
    .in0(multiplexer_1_out), .in1({5{1'b1}}), .out(multiplexer_3_out), .sel(jal));
  Multiplexer #(.width(32), .enable("false")) multiplexer_4 (
    .in0(bit_extender_1_out), .in1(bit_extender_2_out), .out(multiplexer_4_out), .sel(EXTOP));
  Multiplexer #(.width(32), .enable("false")) multiplexer_5 (
    .in0(multiplexer_6_out), .in1(RF_A), .out(multiplexer_5_out), .sel(jr));
  // RegisterFile registerfile_1: pin names not known; wires that end beside it: multiplexer_2_out, RegWrite, multiplexer_3_out, rom_1_data[25:21], rom_1_data[20:16], RF_A, registerfile_1_p7
  or or_1 (or_1_out, j, jal);
  Multiplexer #(.width(32), .enable("false")) multiplexer_6 (
    .in0(multiplexer_9_out), .in1(PC31__28__instr_index__02), .out(multiplexer_6_out), .sel(or_1_out));
  Multiplexer #(.width(32), .enable("false")) multiplexer_7 (
    .in0(registerfile_1_p7), .in1(multiplexer_4_out), .out(multiplexer_7_out), .sel(ALUsrc));
  Shifter #(.width(32)) shifter_1 (.in(multiplexer_4_out), .\dist (5'b00010), .out(shifter_1_out));
  Multiplexer #(.width(32), .enable("false")) multiplexer_8 (
    .in0(alu_1_p5), .in1(ram_1_data), .out(multiplexer_8_out), .sel(MemToReg));
  // ALU alu_1: pin names not known; wires that end beside it: RF_A, multiplexer_7_out, ALUOP, alu_1_p4, alu_1_p5
  Adder #(.width(32)) adder_2 (.a(adder_1_out), .b(shifter_1_out), .out(adder_2_out));  // open: cin, cout
  Multiplexer #(.width(32), .enable("false")) multiplexer_9 (
    .in0(adder_1_out), .in1(adder_2_out), .out(multiplexer_9_out), .sel(or_2_out));
  or or_2 (or_2_out, and_1_out, and_2_out, and_3_out);
  and and_1 (and_1_out, not_1_out, blez);
  and and_2 (and_2_out, alu_1_p4, beq);
  and and_3 (and_3_out, not_2_out, bne);
  RAM #(.addrWidth(16), .dataWidth(32), .bus("separate")) ram_1 (
    .addr(alu_1_p5[15:0]), .din(registerfile_1_p7), .data(ram_1_data), .str(Memwrite));  // open: sel, clk, ld, clr
  not not_1 (not_1_out, comparator_1_gt);
  not not_2 (not_2_out, alu_1_p4);
  Comparator #(.width(32)) comparator_1 (.a(RF_A), .b({32{1'b0}}), .gt(comparator_1_gt));  // open: eq, lt

  // Notes on the sheet:
  //   数码管输出应该用寄存器锁存，否则显示数据只能一闪而过
  //   指令存储器
  //   可以通过项目增加Logisim库的方式将前几次实验完成的电路作为子电路引入到本电路中使用
  //   数码管输出
  //   总复位信号应将除ROM以外所有存储组件全部清零
  //   寄存器文件
  //   数据存储器
endmodule

module controller (
  input  [5:0] func,
  input  [5:0] op,
  output RegDst,
  output ALUsrc,
  output PCsrc,
  output MemWrite,
  output MemToReg,
  output RegWrite,
  output Jump,
  output [3:0] ALUOP
);

  wire add_out, addi_out, addiu_out, addu_out, and_out, andi_out, beq_out, blez_out, bne_out, j_out, jal_out,
       jr_out, lw_out, nor_out, not_1_out, not_2_out, not_3_out, not_4_out, not_5_out, not_6_out, not_7_out,
       not_8_out, not_9_out, not_10_out, not_11_out, not_12_out, or_out, ori_out, sh_out, sll_out, slt_out,
       slti_out, sltiu_out, sltu_out, sra_out, srl_out, sub_out, sw_out, syscall_out, xor_out;

  not not_1 (not_1_out, func[5]);
  not not_2 (not_2_out, func[3]);
  not not_3 (not_3_out, func[4]);
  not not_4 (not_4_out, func[1]);
  not not_5 (not_5_out, func[2]);
  not not_6 (not_6_out, func[0]);
  not not_7 (not_7_out, op[5]);
  not not_8 (not_8_out, op[4]);
  not not_9 (not_9_out, op[3]);
  not not_10 (not_10_out, op[2]);
  not not_11 (not_11_out, op[0]);
  not not_12 (not_12_out, op[1]);
  and add (add_out, not_7_out, not_8_out, not_9_out, not_10_out, not_12_out, not_11_out, func[5], not_3_out, not_2_out, not_5_out, not_4_out, not_6_out);
  and addi (addi_out, not_7_out, not_8_out, op[3], not_10_out, not_12_out, not_11_out);
  and addiu (addiu_out, not_7_out, not_8_out, op[3], not_10_out, not_12_out, op[0]);
  and addu (addu_out, not_7_out, not_8_out, not_9_out, not_10_out, not_12_out, not_11_out, func[5], not_3_out, not_2_out, not_5_out, not_4_out, func[0]);
  and \and  (and_out, not_7_out, not_8_out, not_9_out, not_10_out, not_12_out, not_11_out, func[5], not_3_out, not_2_out, func[2], not_4_out, not_6_out);
  and andi (andi_out, not_7_out, not_8_out, op[3], op[2], not_12_out, not_11_out);
  and sll (sll_out, not_7_out, not_8_out, not_9_out, not_10_out, not_12_out, not_11_out, not_1_out, not_3_out, not_2_out, not_5_out, not_4_out, not_6_out);
  and sra (sra_out, not_7_out, not_8_out, not_9_out, not_10_out, not_12_out, not_11_out, not_1_out, not_3_out, not_2_out, not_5_out, func[1], func[0]);
  and srl (srl_out, not_7_out, not_8_out, not_9_out, not_10_out, not_12_out, not_11_out, not_1_out, not_3_out, not_2_out, not_5_out, func[1], not_6_out);
  and sub (sub_out, not_7_out, not_8_out, not_9_out, not_10_out, not_12_out, not_11_out, func[5], not_3_out, not_2_out, not_5_out, func[1], not_6_out);
  and \or  (or_out, not_7_out, not_8_out, not_9_out, not_10_out, not_12_out, not_11_out, func[5], not_3_out, not_2_out, func[2], not_4_out, func[0]);
  and ori (ori_out, not_7_out, not_8_out, op[3], op[2], not_12_out, op[0]);
  and \nor  (nor_out, not_7_out, not_8_out, not_9_out, not_10_out, not_12_out, not_11_out, func[5], not_3_out, not_2_out, func[2], func[1], func[0]);
  and lw (lw_out, op[5], not_8_out, not_9_out, not_10_out, op[1], op[0]);
  and sw (sw_out, op[5], not_8_out, op[3], not_10_out, op[1], op[0]);
  and beq (beq_out, not_7_out, not_8_out, not_9_out, op[2], not_12_out, not_11_out);
  and bne (bne_out, not_7_out, not_8_out, not_9_out, op[2], not_12_out, op[0]);
  and slt (slt_out, not_7_out, not_8_out, not_9_out, not_10_out, not_12_out, not_11_out, func[5], not_3_out, func[3], not_5_out, func[1], not_6_out);
  and slti (slti_out, not_7_out, not_8_out, op[3], not_10_out, op[1], not_11_out);
  and sltu (sltu_out, not_7_out, not_8_out, not_9_out, not_10_out, not_12_out, not_11_out, func[5], not_3_out, func[3], not_5_out, func[1], func[0]);
  and j (j_out, not_7_out, not_8_out, not_9_out, not_10_out, op[1], not_11_out);
  and jal (jal_out, not_7_out, not_8_out, not_9_out, not_10_out, op[1], op[0]);
  and jr (jr_out, not_7_out, not_8_out, not_9_out, not_10_out, not_12_out, not_11_out, not_1_out, not_3_out, func[3], not_5_out, not_4_out, not_6_out);
  and syscall (syscall_out, not_7_out, not_8_out, not_9_out, not_10_out, not_12_out, not_11_out, not_1_out, not_3_out, func[3], func[2], not_4_out, not_6_out);
  and \xor  (xor_out, not_7_out, not_8_out, not_9_out, not_10_out, not_12_out, not_11_out, func[5], not_3_out, not_2_out, func[2], func[1], not_6_out);
  and sltiu (sltiu_out, not_7_out, not_8_out, op[3], not_10_out, op[1], op[0]);
  and sh (sh_out, op[5], not_8_out, op[3], not_10_out, not_12_out, op[0]);
  and blez (blez_out, not_7_out, not_8_out, not_9_out, op[2], op[1], not_11_out);
  or or_2 (RegDst, add_out, addu_out, and_out, sll_out, sra_out, srl_out, sub_out, or_out, nor_out, slt_out, sltu_out, xor_out);
  or or_3 (ALUsrc, addi_out, addiu_out, andi_out, sll_out, sra_out, srl_out, ori_out, lw_out, sw_out, slti_out, sltiu_out, sh_out);
  // OR_Gate or_4 has open pins: out=PCsrc
  // OR_Gate or_5 has open pins: out=MemWrite
  // OR_Gate or_6 has open pins: out=MemToReg
  // OR_Gate or_7 has open pins: out=RegWrite
  // OR_Gate or_8 has open pins: out=Jump
endmodule
