// Logisim project CS1503_U201514559_周铭昊_CPU.circ as structural Verilog: 4 circuits, main circuit cpu
module cpu (
);

  wire alu_1_p4, ALUsrc, and_1_out, and_2_out, and_3_out, and_4_out, and_5_out, and_6_out, and_7_out,
       and_8_out, and_9_out, beq, blez, bne, CLK, comparator_1_eq, comparator_2_eq, comparator_4_eq,
       comparator_5_gt, correct_b, halt, j, jal, jr, MemToReg, Memwrite, not_1_out, not_2_out, not_3_out,
       not_4_out, not_5_out, not_6_out, not_7_out, not_8_out, or_2_out, or_3_out, or_5_out, RegDst,
       register_1_q, RegWrite, RST, S, sh, Syscall;
  wire [1:0] EXTOP;
  wire [3:0] ALUOP;
  wire [4:0] multiplexer_1_out, multiplexer_2_out, multiplexer_3_out, multiplexer_5_out, multiplexer_6_out;
  wire [9:0] PC_q;
  wire [15:0] \总周期数 , \无条件分支指令数 , \有条件分支成功跳转 , \有条件分支指令数 ;
  wire [21:0] PC_q_2;
  wire [25:0] index;
  wire [31:0] adder_1_out, adder_2_out, alu_1_p5, bit_extender_1_out, bit_extender_2_out, bit_extender_3_out,
       multiplexer_4_out, multiplexer_7_out, multiplexer_8_out, multiplexer_9_out, multiplexer_10_out,
       multiplexer_11_out, multiplexer_12_out, multiplexer_13_out, multiplexer_14_out, ram_1_data,
       register_2_q, registerfile_1_p8, RF_A, SyscallOut;
  wire [31:26] rom_1_data;

  Button \u_总复位  (.out(RST));
  Clock clock_1 (.out(CLK));
  not not_1 (not_1_out, halt);
  Register #(.width(32)) PC (.D(multiplexer_7_out), .en(not_1_out), .Q({PC_q_2, PC_q}), .clk(CLK), .clr(RST));
  Comparator #(.width(32)) comparator_1 (.a(RF_A), .b(32'ha), .eq(comparator_1_eq));  // open: gt, lt
  Hex_Digit_Display hex_digit_display_1 (.value(SyscallOut[27:24]));  // open: dp
  Hex_Digit_Display hex_digit_display_2 (.value(SyscallOut[31:28]));  // open: dp
  Adder #(.width(32)) adder_1 (.a(32'h1), .b({PC_q_2, PC_q}), .out(adder_1_out));  // open: cin, cout
  ROM #(.addrWidth(10), .dataWidth(32)) rom_1 (.addr(PC_q), .data({rom_1_data, index}));  // open: sel
  Hex_Digit_Display hex_digit_display_3 (.value(SyscallOut[19:16]));  // open: dp
  Hex_Digit_Display hex_digit_display_4 (.value(SyscallOut[23:20]));  // open: dp
  Comparator #(.width(32), .mode("unsigned")) comparator_2 (
    .a({rom_1_data, index}), .b({32{1'b0}}), .eq(comparator_2_eq));  // open: gt, lt
  and and_1 (and_1_out, comparator_1_eq, Syscall);
  Hex_Digit_Display hex_digit_display_5 (.value(SyscallOut[15:12]));  // open: dp
  Hex_Digit_Display hex_digit_display_6 (.value(SyscallOut[11:8]));  // open: dp
  // Probe on rom_1_data
  // Probe on index[5:0]
  or or_1 (halt, comparator_2_eq, and_1_out);
  Hex_Digit_Display hex_digit_display_7 (.value(SyscallOut[3:0]));  // open: dp
  Hex_Digit_Display hex_digit_display_8 (.value(SyscallOut[7:4]));  // open: dp
  controller controller_1 (
    .func(index[5:0]), .op(rom_1_data), .RegDst(RegDst), .ALUsrc(ALUsrc), .blez(blez), .MemWrite(Memwrite),
    .RegWrite(RegWrite), .ALUOP(ALUOP), .MemToReg(MemToReg), .EXTOP(EXTOP), .beq(beq), .bne(bne), .j(j),
    .jal(jal), .jr(jr), .Syscall(Syscall), .sh(sh));
  // Probe on \总周期数 
  // Probe on \无条件分支指令数 
  // Probe on \有条件分支指令数 
  // Probe on \有条件分支成功跳转 
  Multiplexer #(.width(5), .enable("false")) multiplexer_1 (
    .in0(index[25:21]), .in1(index[20:16]), .out(multiplexer_1_out), .sel(S));
  Multiplexer #(.width(5), .enable("false")) multiplexer_2 (
    .in0(index[20:16]), .in1(index[15:11]), .out(multiplexer_2_out), .sel(RegDst));
  Multiplexer #(.width(5), .enable("false")) multiplexer_3 (
    .in0(multiplexer_1_out), .in1(5'b00010), .out(multiplexer_3_out), .sel(Syscall));
  assign bit_extender_1_out = {{16{index[15]}}, index[15:0]};  // Bit_Extender bit_extender_1
  assign bit_extender_2_out = {{16{1'b0}}, index[15:0]};  // Bit_Extender bit_extender_2
  assign bit_extender_3_out = {{27{1'b0}}, index[10:6]};  // Bit_Extender bit_extender_3
  not not_2 (not_2_out, halt);
  Multiplexer #(.width(32), .enable("false")) multiplexer_4 (
    .in0(multiplexer_11_out), .in1(adder_1_out), .out(multiplexer_4_out), .sel(jal));
  Multiplexer #(.width(5), .enable("false")) multiplexer_5 (
    .in0(index[20:16]), .in1(5'b00100), .out(multiplexer_5_out), .sel(Syscall));
  Multiplexer #(.width(5), .enable("false")) multiplexer_6 (
    .in0(multiplexer_2_out), .in1({5{1'b1}}), .out(multiplexer_6_out), .sel(jal));
  Comparator #(.width(2), .mode("unsigned")) comparator_3 (.a(EXTOP), .b(2'b10), .eq(S));  // open: gt, lt
  Counter #(.width(16), .max('hffff)) counter_1 (
    .D(16'h1), .Q(\总周期数 ), .clk(and_2_out), .clr(RST));  // open: load, count, carry
  and and_2 (and_2_out, register_1_q, CLK);
  Register #(.width(1)) register_1 (.D(not_2_out), .Q(register_1_q), .clk(CLK), .clr(RST));  // open: en
  Multiplexer #(.width(32), .enable("false")) multiplexer_7 (
    .in0(multiplexer_9_out), .in1(RF_A), .out(multiplexer_7_out), .sel(jr));
  Multiplexer #(.select(2), .width(32), .enable("false")) multiplexer_8 (
    .in0(bit_extender_1_out), .in1(bit_extender_2_out), .in2(bit_extender_3_out), .in3({32{1'b0}}),
    .out(multiplexer_8_out), .sel(EXTOP));
  // RegisterFile registerfile_1: pin names not known; wires that end beside it: multiplexer_4_out, CLK, RegWrite, multiplexer_6_out, multiplexer_3_out, multiplexer_5_out, RF_A, registerfile_1_p8
  or or_2 (or_2_out, j, jal);
  Multiplexer #(.width(32), .enable("false")) multiplexer_9 (
    .in0(multiplexer_13_out), .in1({{6{1'b0}}, index}), .out(multiplexer_9_out), .sel(or_2_out));
  Multiplexer #(.width(32), .enable("false")) multiplexer_10 (
    .in0(registerfile_1_p8), .in1(multiplexer_8_out), .out(multiplexer_10_out), .sel(ALUsrc));
  or or_3 (or_3_out, j, jal, jr);
  Multiplexer #(.width(32), .enable("false")) multiplexer_11 (
    .in0(alu_1_p5), .in1(ram_1_data), .out(multiplexer_11_out), .sel(MemToReg));
  // ALU alu_1: pin names not known; wires that end beside it: RF_A, multiplexer_10_out, ALUOP, alu_1_p4, alu_1_p5
  Multiplexer #(.width(32), .enable("false")) multiplexer_12 (
    .in0(registerfile_1_p8), .in1({{16{1'b0}}, registerfile_1_p8[15:0]}), .out(multiplexer_12_out), .sel(sh));
  Comparator #(.width(32), .mode("unsigned")) comparator_4 (.a(RF_A), .b(32'ha), .eq(comparator_4_eq));  // open: gt, lt
  Counter #(.width(16), .max('hffff)) counter_2 (
    .D(16'h1), .Q(\无条件分支指令数 ), .clk(and_3_out), .clr(RST));  // open: load, count, carry
  and and_3 (and_3_out, or_3_out, not_3_out);
  not not_3 (not_3_out, CLK);
  Adder #(.width(32)) adder_2 (.a(adder_1_out), .b(multiplexer_8_out), .out(adder_2_out));  // open: cin, cout
  not not_4 (not_4_out, comparator_4_eq);
  Multiplexer #(.width(32), .enable("false")) multiplexer_13 (
    .in0(adder_1_out), .in1(adder_2_out), .out(multiplexer_13_out), .sel(correct_b));
  or or_4 (correct_b, and_5_out, and_6_out, and_7_out);
  and and_4 (and_4_out, not_4_out, Syscall);
  Multiplexer #(.width(32), .enable("false")) multiplexer_14 (
    .in0(register_2_q), .in1(registerfile_1_p8), .out(multiplexer_14_out), .sel(and_4_out));
  and and_5 (and_5_out, not_6_out, blez);
  and and_6 (and_6_out, alu_1_p4, beq);
  and and_7 (and_7_out, not_7_out, bne);
  RAM #(.addrWidth(16), .dataWidth(32), .bus("separate")) ram_1 (
    .addr(alu_1_p5[15:0]), .din(multiplexer_12_out), .data(ram_1_data), .str(Memwrite), .clk(CLK),
    .ld(MemToReg), .clr(RST));  // open: sel
  Counter #(.width(16), .max('hffff)) counter_3 (
    .D(16'h1), .Q(\有条件分支指令数 ), .clk(and_8_out), .clr(RST));  // open: load, count, carry
  and and_8 (and_8_out, or_5_out, not_5_out);
  or or_5 (or_5_out, blez, beq, bne);
  not not_5 (not_5_out, CLK);
  not not_6 (not_6_out, comparator_5_gt);
  not not_7 (not_7_out, alu_1_p4);
  Register #(.width(32)) register_2 (.D(multiplexer_14_out), .en(1'b1), .Q(register_2_q), .clk(CLK), .clr(RST));
  Comparator #(.width(32), .mode("unsigned")) comparator_5 (
    .a(RF_A), .b({32{1'b0}}), .gt(comparator_5_gt));  // open: eq, lt
  Multiplexer #(.width(32), .enable("false")) multiplexer_15 (
    .in0(register_2_q), .in1(multiplexer_14_out), .out(SyscallOut), .sel(and_4_out));
  Counter #(.width(16), .max('hffff)) counter_4 (
    .D(16'h1), .Q(\有条件分支成功跳转 ), .clk(and_9_out), .clr(RST));  // open: load, count, carry
  and and_9 (and_9_out, correct_b, not_8_out);
  not not_8 (not_8_out, CLK);

  // Notes on the sheet:
  //   指令存储器
  //   数码管输出应该用寄存器锁存，否则显示数据只能一闪而过
  //   contents of rom_1 (hex, n*v repeats v):
  //   20110001 8000c05 20110001 20120002 20130003 8000c09 20110001 20120002 20130003 8000c0d 20110001
  //   20120002 20130003 8000c11 20110001 20120002 20130003 c000cb8 20100001 20110001 118fc0 112020
  //   20020022 c 118882 12200001 8000c15 112020 20020022 c 20110001 118880 112020 20020022 c 12200001
  //   8000c1f 20110001 118fc0 112020 20020022 c 1188c3 112020 20020022 c 118903 112020 20020022 c 118903
  //   112020 20020022 c 118903 112020 20020022 c 118903 112020 20020022 c 118903 112020 20020022 c 118903
  //   112020 20020022 c 118903 112020 20020022 c 20100001 109fc0 139fc3 8021 2012000c 24160003 26100001
  //   3210000f 20080008 20090001 139900 2709825 132020 20020022 c 1094022 1500fff9 22100001 2018000f
  //   2188024 108700 20080008 20090001 139902 2709825 132021 20020022 c 1094022 1500fff9 108702 2c9b022
  //   12c00001 8000c50 4020 1084027 84400 3508ffff 82021 20020022 c 2010ffff 20110000 ae300000 22100001
  //   22310004 ae300000 22100001 22310004 ae300000 22100001 22310004 ae300000 22100001 22310004 ae300000
  //   22100001 22310004 ae300000 22100001 22310004 ae300000 22100001 22310004 ae300000 22100001 22310004
  //   ae300000 22100001 22310004 ae300000 22100001 22310004 ae300000 22100001 22310004 ae300000 22100001
  //   22310004 ae300000 22100001 22310004 ae300000 22100001 22310004 ae300000 22100001 22310004 ae300000
  //   22100001 22310004 22100001 8020 2011003c 8e130000 8e340000 274402a 11000002 ae330000 ae140000
  //   2231fffc 1611fff8 102020 20020022 c 22100004 2011003c 1611fff2 2002000a c 20100000 22100001 102020
  //   20020022 c 22100002 102020 20020022 c 22100003 102020 20020022 c 22100004 102020 20020022 c 22100005
  //   102020 20020022 c 22100006 102020 20020022 c 22100007 102020 20020022 c 22100008 102020 20020022
  //   20020022 c 3e00008
  //   可以通过项目增加Logisim库的方式将前几次实验完成的电路作为子电路引入到本电路中使用
  //   数码管输出
  //   总复位信号应将除ROM以外所有存储组件全部清零
  //   控制器
  //   寄存器文件
  //   数据存储器
endmodule

module controller (
  input  [5:0] func,
  input  [5:0] op,
  output RegDst,
  output ALUsrc,
  output RegWrite,
  output MemToReg,
  output MemWrite,
  output [1:0] EXTOP,
  output blez,
  output beq,
  output bne,
  output j,
  output jal,
  output jr,
  output Syscall,
  output [3:0] ALUOP,
  output sh
);

  wire add, add_out, addi_out, addiu_out, addu_out, \and , and_out, andi_out, \nor , not_1_out, not_2_out,
       not_3_out, not_4_out, not_5_out, not_6_out, not_7_out, not_8_out, not_9_out, not_10_out, not_11_out,
       not_12_out, not_13_out, not_14_out, not_15_out, not_16_out, not_17_out, not_18_out, not_19_out,
       not_20_out, not_21_out, not_22_out, not_23_out, \or , or_out, sll, slt, slt_out, slti_out, sltiu_out,
       sltu, sltu_out, sra, srl, sub, sw_out, \xor ;

  not not_1 (not_1_out, func[5]);
  not not_2 (not_2_out, func[3]);
  not not_3 (not_3_out, func[4]);
  not not_4 (not_4_out, func[2]);
  not not_5 (not_5_out, func[1]);
  not not_6 (not_6_out, func[0]);
  not not_7 (not_7_out, op[4]);
  not not_8 (not_8_out, op[5]);
  not not_9 (not_9_out, op[3]);
  not not_10 (not_10_out, op[2]);
  not not_11 (not_11_out, op[0]);
  not not_12 (not_12_out, op[1]);
  and u_add (add_out, not_8_out, not_7_out, not_9_out, not_10_out, not_12_out, not_11_out, func[5], not_3_out, not_2_out, not_4_out, not_5_out, not_6_out);
  and addi (addi_out, not_8_out, not_7_out, op[3], not_10_out, not_12_out, not_11_out);
  and addiu (addiu_out, not_8_out, not_7_out, op[3], not_10_out, not_12_out, op[0]);
  and addu (addu_out, not_8_out, not_7_out, not_9_out, not_10_out, not_12_out, not_11_out, func[5], not_3_out, not_2_out, not_4_out, not_5_out, func[0]);
  and u_and (and_out, not_8_out, not_7_out, not_9_out, not_10_out, not_12_out, not_11_out, func[5], not_3_out, not_2_out, func[2], not_5_out, not_6_out);
  and andi (andi_out, not_8_out, not_7_out, op[3], op[2], not_12_out, not_11_out);
  and u_sll (sll, not_8_out, not_7_out, not_9_out, not_10_out, not_12_out, not_11_out, not_1_out, not_3_out, not_2_out, not_4_out, not_5_out, not_6_out);
  and u_sra (sra, not_8_out, not_7_out, not_9_out, not_10_out, not_12_out, not_11_out, not_1_out, not_3_out, not_2_out, not_4_out, func[1], func[0]);
  and u_srl (srl, not_8_out, not_7_out, not_9_out, not_10_out, not_12_out, not_11_out, not_1_out, not_3_out, not_2_out, not_4_out, func[1], not_6_out);
  and u_sub (sub, not_8_out, not_7_out, not_9_out, not_10_out, not_12_out, not_11_out, func[5], not_3_out, not_2_out, not_4_out, func[1], not_6_out);
  and u_or (or_out, not_8_out, not_7_out, not_9_out, not_10_out, not_12_out, not_11_out, func[5], not_3_out, not_2_out, func[2], not_5_out, func[0]);
  and ori (EXTOP[0], not_8_out, not_7_out, op[3], op[2], not_12_out, op[0]);
  and u_nor (\nor , not_8_out, not_7_out, not_9_out, not_10_out, not_12_out, not_11_out, func[5], not_3_out, not_2_out, func[2], func[1], func[0]);
  and lw (MemToReg, op[5], not_7_out, not_9_out, not_10_out, op[1], op[0]);
  and sw (sw_out, op[5], not_7_out, op[3], not_10_out, op[1], op[0]);
  and u_beq (beq, not_8_out, not_7_out, not_9_out, op[2], not_12_out, not_11_out);
  and u_bne (bne, not_8_out, not_7_out, not_9_out, op[2], not_12_out, op[0]);
  and u_slt (slt_out, not_8_out, not_7_out, not_9_out, not_10_out, not_12_out, not_11_out, func[5], not_3_out, func[3], not_4_out, func[1], not_6_out);
  and slti (slti_out, not_8_out, not_7_out, op[3], not_10_out, op[1], not_11_out);
  and u_sltu (sltu_out, not_8_out, not_7_out, not_9_out, not_10_out, not_12_out, not_11_out, func[5], not_3_out, func[3], not_4_out, func[1], func[0]);
  and u_j (j, not_8_out, not_7_out, not_9_out, not_10_out, op[1], not_11_out);
  and u_jal (jal, not_8_out, not_7_out, not_9_out, not_10_out, op[1], op[0]);
  and u_jr (jr, not_8_out, not_7_out, not_9_out, not_10_out, not_12_out, not_11_out, not_1_out, not_3_out, func[3], not_4_out, not_5_out, not_6_out);
  and u_syscall (Syscall, not_8_out, not_7_out, not_9_out, not_10_out, not_12_out, not_11_out, not_1_out, not_3_out, func[3], func[2], not_5_out, not_6_out);
  and u_xor (\xor , not_8_out, not_7_out, not_9_out, not_10_out, not_12_out, not_11_out, func[5], not_3_out, not_2_out, func[2], func[1], not_6_out);
  and sltiu (sltiu_out, not_8_out, not_7_out, op[3], not_10_out, op[1], op[0]);
  and u_sh (sh, op[5], not_7_out, op[3], not_10_out, not_12_out, op[0]);
  and u_blez (blez, not_8_out, not_7_out, not_9_out, op[2], op[1], not_11_out);
  or or_2 (RegDst, add_out, addu_out, and_out, sll, sra, srl, sub, or_out, \nor , slt_out, sltu_out, \xor );
  or or_3 (ALUsrc, addi_out, addiu_out, andi_out, sll, sra, srl, EXTOP[0], MemToReg, sw_out, slti_out, sltiu_out, sh);
  or or_4 (RegWrite, add_out, addi_out, addiu_out, addu_out, and_out, andi_out, sll, sra, srl, sub, or_out, EXTOP[0], \nor , MemToReg, slt_out, slti_out, sltu_out, jal, \xor , sltiu_out);
  or or_5 (MemWrite, sw_out, sh);
  or or_6 (EXTOP[1], sll, sra, srl);
  or and_2 (\and , and_out, andi_out);
  or or_7 (\or , or_out, EXTOP[0]);
  or slt_2 (slt, slt_out, slti_out);
  or ALUOP3 (ALUOP[3], \or , \xor , \nor , slt, sltu);
  or ALUOP2 (ALUOP[2], add, sub, \and , sltu);
  or ALUOP1 (ALUOP[1], srl, sub, \and , \nor , slt);
  or ALUOP0 (ALUOP[0], sra, add, \and , \xor , slt);
  or sltu_2 (sltu, sltu_out, sltiu_out);
  not not_13 (not_13_out, sra);
  not not_14 (not_14_out, sll);
  or add_2 (add, add_out, addi_out, addiu_out, addu_out, MemToReg, sw_out, sh);
  not not_15 (not_15_out, srl);
  not not_16 (not_16_out, add);
  not not_17 (not_17_out, \and );
  not not_18 (not_18_out, sub);
  not not_19 (not_19_out, \or );
  not not_20 (not_20_out, \xor );
  not not_21 (not_21_out, \nor );
  not not_22 (not_22_out, slt);
  not not_23 (not_23_out, sltu);
endmodule

module IF_ID (
  input  [31:0] PC_4,
  input  [31:0] \指令 ,
  input  in_3,
  input  in_4,
  output [31:0] PC_4_2,
  output [31:0] \指令_2 
);

  wire [31:0] multiplexer_1_out, multiplexer_2_out;

  Multiplexer #(.width(32), .enable("false")) multiplexer_1 (
    .in0(PC_4), .in1({32{1'b0}}), .out(multiplexer_1_out), .sel(in_3));
  Multiplexer #(.width(32), .enable("false")) multiplexer_2 (
    .in0(\指令 ), .in1({32{1'b0}}), .out(multiplexer_2_out), .sel(in_3));
  Register #(.width(32)) register_1 (.D(multiplexer_1_out), .Q(PC_4_2), .clk(in_4));  // open: en, clr
  Register #(.width(32)) register_2 (.D(multiplexer_2_out), .Q(\指令_2 ), .clk(in_4));  // open: en, clr

  // Other names for the same wires on the sheet: CLK = in_4; RST = in_3
endmodule

module ID_EX (
  input  in_1,
  input  in_2,
  input  [31:0] PC_4,
  input  [31:0] \指令 ,
  input  RegDst,
  input  ALUsrc,
  input  RegWrite,
  input  MemToReg,
  input  MemWrite,
  input  [1:0] EXTOP,
  input  blez,
  input  beq,
  input  bne,
  input  j,
  input  jal,
  input  jr,
  input  Syscall,
  input  [3:0] ALUOP,
  output [31:0] PC_4_2,
  output [31:0] \指令_2 ,
  output RegDst_2,
  output ALUsrc_2,
  output RegWrite_2,
  output MemToReg_2,
  output MemWrite_2,
  output [1:0] EXTOP_2,
  output blez_2,
  output beq_2,
  output bne_2,
  output j_2,
  output jal_2,
  output jr_2,
  output Syscall_2,
  output [3:0] ALUOP_2
);

  wire multiplexer_3_out, multiplexer_4_out, multiplexer_5_out, multiplexer_6_out, multiplexer_7_out,
       multiplexer_9_out, multiplexer_10_out, multiplexer_11_out, multiplexer_12_out, multiplexer_13_out,
       multiplexer_14_out, multiplexer_15_out;
  wire [1:0] multiplexer_8_out;
  wire [3:0] multiplexer_16_out;
  wire [31:0] multiplexer_1_out, multiplexer_2_out;

  Multiplexer #(.width(32), .enable("false")) multiplexer_1 (
    .in0(PC_4), .in1({32{1'b0}}), .out(multiplexer_1_out), .sel(in_1));
  Multiplexer #(.width(32), .enable("false")) multiplexer_2 (
    .in0(\指令 ), .in1({32{1'b0}}), .out(multiplexer_2_out), .sel(in_1));
  Multiplexer #(.enable("false")) multiplexer_3 (.in0(RegDst), .in1(1'b0), .out(multiplexer_3_out), .sel(in_1));
  Multiplexer #(.enable("false")) multiplexer_4 (.in0(ALUsrc), .in1(1'b0), .out(multiplexer_4_out), .sel(in_1));
  Multiplexer #(.enable("false")) multiplexer_5 (.in0(RegWrite), .in1(1'b0), .out(multiplexer_5_out), .sel(in_1));
  Multiplexer #(.enable("false")) multiplexer_6 (.in0(MemToReg), .in1(1'b0), .out(multiplexer_6_out), .sel(in_1));
  Multiplexer #(.enable("false")) multiplexer_7 (.in0(MemWrite), .in1(1'b0), .out(multiplexer_7_out), .sel(in_1));
  Multiplexer #(.width(2), .enable("false")) multiplexer_8 (
    .in0(EXTOP), .in1(2'b00), .out(multiplexer_8_out), .sel(in_1));
  Multiplexer #(.enable("false")) multiplexer_9 (.in0(blez), .in1(1'b0), .out(multiplexer_9_out), .sel(in_1));
  Multiplexer #(.enable("false")) multiplexer_10 (.in0(beq), .in1(1'b0), .out(multiplexer_10_out), .sel(in_1));
  Multiplexer #(.enable("false")) multiplexer_11 (.in0(bne), .in1(1'b0), .out(multiplexer_11_out), .sel(in_1));
  Multiplexer #(.enable("false")) multiplexer_12 (.in0(j), .in1(1'b0), .out(multiplexer_12_out), .sel(in_1));
  Multiplexer #(.enable("false")) multiplexer_13 (.in0(jal), .in1(1'b0), .out(multiplexer_13_out), .sel(in_1));
  Multiplexer #(.enable("false")) multiplexer_14 (.in0(jr), .in1(1'b0), .out(multiplexer_14_out), .sel(in_1));
  Multiplexer #(.enable("false")) multiplexer_15 (.in0(Syscall), .in1(1'b0), .out(multiplexer_15_out), .sel(in_1));
  Multiplexer #(.width(4), .enable("false")) multiplexer_16 (
    .in0(ALUOP), .in1(4'b0000), .out(multiplexer_16_out), .sel(in_1));
  Register #(.width(32)) register_1 (.D(multiplexer_1_out), .Q(PC_4_2), .clk(in_2));  // open: en, clr
  Register #(.width(32)) register_2 (.D(multiplexer_2_out), .Q(\指令_2 ), .clk(in_2));  // open: en, clr
  Register #(.width(1)) register_3 (.D(multiplexer_3_out), .Q(RegDst_2), .clk(in_2));  // open: en, clr
  Register #(.width(1)) register_4 (.D(multiplexer_4_out), .Q(ALUsrc_2), .clk(in_2));  // open: en, clr
  Register #(.width(1)) register_5 (.D(multiplexer_5_out), .Q(RegWrite_2), .clk(in_2));  // open: en, clr
  Register #(.width(1)) register_6 (.D(multiplexer_6_out), .Q(MemToReg_2), .clk(in_2));  // open: en, clr
  Register #(.width(1)) register_7 (.D(multiplexer_7_out), .Q(MemWrite_2), .clk(in_2));  // open: en, clr
  Register #(.width(2)) register_8 (.D(multiplexer_8_out), .Q(EXTOP_2), .clk(in_2));  // open: en, clr
  Register #(.width(1)) register_9 (.D(multiplexer_9_out), .Q(blez_2), .clk(in_2));  // open: en, clr
  Register #(.width(1)) register_10 (.D(multiplexer_10_out), .Q(beq_2), .clk(in_2));  // open: en, clr
  Register #(.width(1)) register_11 (.D(multiplexer_11_out), .Q(bne_2), .clk(in_2));  // open: en, clr
  Register #(.width(1)) register_12 (.D(multiplexer_12_out), .Q(j_2), .clk(in_2));  // open: en, clr
  Register #(.width(1)) register_13 (.D(multiplexer_13_out), .Q(jal_2), .clk(in_2));  // open: en, clr
  Register #(.width(1)) register_14 (.D(multiplexer_14_out), .Q(jr_2), .clk(in_2));  // open: en, clr
  Register #(.width(1)) register_15 (.D(multiplexer_15_out), .Q(Syscall_2), .clk(in_2));  // open: en, clr
  Register #(.width(4)) register_16 (.D(multiplexer_16_out), .Q(ALUOP_2), .clk(in_2));  // open: en, clr

  // Other names for the same wires on the sheet: CLK = in_2; RST = in_1
endmodule
